# Fritzing sketch システム例 (saved by Fritzing 0.9.2b)
stripboards: 1

parts:
  パーツ1 = Arduino Uno (Rev3)  # not connected
  Raspberry_Pi1 = Raspberry Pi 2  # not connected
  Grove4 = Grove 3 Axis Digital Accelerometer 16g  # not connected
  Grove5 = Grove Infrared Emitter  # not connected
  DHT2 = DHT11 Humitidy and Temperature Sensor
  R2 = Resistor [tolerance=±5% resistance=10k package=THT]
  JP4 = Grove Header 4pin Straight direct mount [package=straight]

nets:
  N1: DHT2.VDD, R2.Pin_0, JP4.2
  N2: DHT2.DATA, R2.Pin_1, JP4.4
  N3: DHT2.NULL, JP4.3
  N4: DHT2.GND, JP4.1

notes:
  センサ端末
  Grove用センサ
  Arduino本体
  Groveシールド
  Raspberry Pi
  ロガー用端末
  USBケーブル

custom parts:
  DHT11 Humitidy and Temperature Sensor: DHT11 Humidity and Temperature Sensor
  Grove Header 4pin Straight direct mount: Header
