# Fritzing sketch 箱用ファンなしシールド (saved by Fritzing 0.9.3b)
perfboards: 1

parts:
  パーツ5 = Real Time Clock Module - DS1307 RTC Breakout Board
  J3 = double row male pin header, 20 pins [form="♂ (male)"]
  J4 = double row male pin header, 20 pins [form="♂ (male)"]
  LED1 = LED - 5mm [color="Green (555nm)" package="5 mm [THT]"]
  LED2 = LED - 5mm [color="Yellow (595nm)" package="5 mm [THT]"]
  S1 = Round Pushbutton
  S2 = Round Pushbutton
  R1 = Resistor [tolerance=±5% resistance=10k package=THT]
  R2 = Resistor [tolerance=±5% resistance=10k package=THT]
  J5 = male pin header, 2 pins [form="♂ (male)"]
  J6 = male pin header, 2 pins [form="♂ (male)"]
  J7 = male pin header, 2 pins [form="♂ (male)"]
  J8 = male pin header, 2 pins [form="♂ (male)"]
  J9 = female pin header, 2 pins [form="♀ (female)"]
  J10 = female pin header, 2 pins [form="♀ (female)"]
  J11 = female pin header, 2 pins [form="♀ (female)"]
  J12 = female pin header, 2 pins [form="♀ (female)"]
  SHT25-realsize1 = StrawberryLinux SHT25 Sensor module
  R3 = Resistor [tolerance=±5% resistance=100 package=THT]
  R4 = Resistor [tolerance=±5% resistance=100 package=THT]
  パーツ6 = MM-FT232

nets:
  N1: パーツ5.5V, J4.pin2
  N2: パーツ5.GND, J3.pin20
  N3: パーツ5.SCL, J3.pin3, SHT25-realsize1.SCL
  N4: パーツ5.SDA, J3.pin1, J3.pin2, SHT25-realsize1.VDD, SHT25-realsize1.SDA
  N5: J3.pin5, SHT25-realsize1.GND
  N6: J3.pin16, J8.pin1
  N7: J3.pin17, J7.pin1
  N8: J3.pin18, J6.pin1
  N9: J3.pin19, J5.pin1
  N10: J4.pin3, R2.Pin_0
  N11: J4.pin4, パーツ6.RXI
  N12: J4.pin5, パーツ6.TXO
  N13: J4.pin7, パーツ6.GND
  N14: J4.pin10, R4.Pin_0
  N15: J4.pin15, R3.Pin_0
  N16: J4.pin17, R1.Pin_0
  N17: LED1.cathode, J10.pin1
  N18: LED1.anode, J10.pin2
  N19: LED2.cathode, J9.pin1
  N20: LED2.anode, J9.pin2
  N21: S1.leg0, J12.pin1
  N22: S1.leg1, J12.pin2
  N23: S2.leg0, J11.pin1
  N24: S2.leg1, J11.pin2
  N25: R1.Pin_1, J6.pin2
  N26: R2.Pin_1, J5.pin2
  N27: J7.pin2, R4.Pin_1
  N28: J8.pin2, R3.Pin_1

notes:
  電池付きRTC
  シリアルコンソール

custom parts:
  MM-FT232: sunhayato MM-FT232
